# Fritzing sketch scara-drawbot (saved by Fritzing 0.9.3b)
circuit board: 8.46667cm x 5.64444cm
breadboards: 1

parts:
  Servo_Shoulder = Basic Servo
  Servo_Elbow = Basic Servo
  Part1 = Arduino Uno (Rev3)
  Part2 = Bluetooth HC-05 Macho

nets:
  GND: Servo_Shoulder.gnd, Servo_Elbow.gnd, Part1.GND, Part2.GND
  VCC: Servo_Shoulder.vcc, Servo_Elbow.vcc, Part1.5V
  N1: Servo_Shoulder.pulse, Part1.D5_PWM
  N2: Servo_Elbow.pulse, Part1.D6_PWM
  N3: Part1.D0/RX, Part2.TXD
  N4: Part1.D1/TX, Part2.RXD
